// Logisim project mult.circ as structural Verilog: 12 circuits, main circuit main
module main (
  output [3:0] out_1,
  output [3:0] out_2,
  output [3:0] out_3,
  output [3:0] out_4,
  output [3:0] out_5,
  output [3:0] out_6,
  output [3:0] out_7,
  output [3:0] out_8,
  output [3:0] out_9,
  output [3:0] out_10,
  output [3:0] out_11,
  output [3:0] out_12,
  output [3:0] out_13,
  output [3:0] out_14,
  output [3:0] out_15,
  output [3:0] out_16,
  output [3:0] out_17,
  output [3:0] out_18,
  output [3:0] out_19,
  output [3:0] out_20,
  output [3:0] out_21,
  output [3:0] out_22,
  output [3:0] out_23,
  output [3:0] out_24,
  output [3:0] out_25,
  output [3:0] out_26,
  output [3:0] out_27,
  output [3:0] out_28,
  output [3:0] out_29,
  output [3:0] out_30,
  output [3:0] out_31,
  output [3:0] out_32
);

  mult mult_1 (.A(2'b00), .B(2'b00), .P(out_1));
  mult mult_2 (.A(2'b00), .B(2'b01), .P(out_5));
  mult mult_3 (.A(2'b00), .B(2'b10), .P(out_9));
  mult mult_4 (.A(2'b00), .B(2'b11), .P(out_13));
  mult mult_5 (.A(2'b01), .B(2'b00), .P(out_17));
  mult mult_6 (.A(2'b01), .B(2'b01), .P(out_21));
  mult mult_7 (.A(2'b01), .B(2'b10), .P(out_25));
  mult mult_8 (.A(2'b01), .B(2'b11), .P(out_29));
  mult mult_9 (.A(2'b10), .B(2'b00), .P(out_2));
  mult mult_10 (.A(2'b10), .B(2'b01), .P(out_6));
  mult mult_11 (.A(2'b10), .B(2'b10), .P(out_10));
  mult mult_12 (.A(2'b10), .B(2'b11), .P(out_14));
  mult mult_13 (.A(2'b11), .B(2'b00), .P(out_18));
  mult mult_14 (.A(2'b11), .B(2'b01), .P(out_22));
  mult mult_15 (.A(2'b11), .B(2'b10), .P(out_26));
  mult mult_16 (.A(2'b11), .B(2'b11), .P(out_30));

  assign out_3 = out_1;
  assign out_4 = out_2;
  assign out_7 = out_5;
  assign out_8 = out_6;
  assign out_11 = out_9;
  assign out_12 = out_10;
  assign out_15 = out_13;
  assign out_16 = out_14;
  assign out_19 = out_17;
  assign out_20 = out_18;
  assign out_23 = out_21;
  assign out_24 = out_22;
  assign out_27 = out_25;
  assign out_28 = out_26;
  assign out_31 = out_29;
  assign out_32 = out_30;
endmodule

module mult (
  input  [1:0] A,
  input  [1:0] B,
  output [3:0] P
);

  wire and_1_out, and_2_out, Y_out;

  and X (P[0], A[0], B[0]);
  and Y (Y_out, A[1], B[1]);
  and P3 (P[3], Y_out, P[0]);
  and P2 (P[2], Y_out, ~P[0]);  // AND_Gate
  and and_1 (and_1_out, B[0], A[1]);
  and and_2 (and_2_out, B[1], A[0]);
  xor P1 (P[1], and_2_out, and_1_out);
endmodule

module mult_sgn (
  input  [1:0] A,
  input  [1:0] B,
  output [3:0] P
);

  wire and_1_out, and_2_out, and_3_out, X_out, Y_out;

  and X (X_out, A[0], B[1]);
  and Y (Y_out, A[1], B[0]);
  and and_1 (and_1_out, Y_out, ~B[1]);  // AND_Gate
  and and_2 (and_2_out, X_out, ~A[1]);  // AND_Gate
  or P3 (P[3], and_1_out, and_2_out);
  or P2 (P[2], P[3], and_3_out);
  and and_3 (and_3_out, B[1], ~B[0], A[1], ~A[0]);  // AND_Gate
  xor P1 (P[1], Y_out, X_out);
  and P0 (P[0], B[0], A[0]);
endmodule

module mult_sgn_6bit (
  input  [2:0] A,
  input  [2:0] B,
  output [5:0] P
);

  wire A10_out, and_1_out, and_2_out, and_3_out, and_4_out, and_5_out, and_6_out, and_7_out, and_8_out,
       and_9_out, and_10_out, and_11_out, and_12_out, B10_out, M10_out, M11_out, nand_1_out, nor_1_out,
       nor_2_out, or_1_out, or_2_out, or_3_out, or_4_out, X22_out;

  and M00 (P[0], A[0], B[0]);
  and M10 (M10_out, A[0], B[1]);
  and X22 (X22_out, ~A[2], B[2]);  // AND_Gate
  and and_1 (and_1_out, B[0], A[1]);
  xor P1 (P[1], M10_out, and_1_out);
  and and_2 (and_2_out, B[2], ~B[0], A[0]);  // AND_Gate
  and and_3 (and_3_out, B[0], A[2], ~A[0]);  // AND_Gate
  or or_1 (or_1_out, and_2_out, and_3_out);
  and and_4 (and_4_out, or_1_out, ~M11_out);  // AND_Gate
  and M11 (M11_out, B[1], A[1]);
  or or_2 (or_2_out, B[2], B[0]);
  and and_5 (and_5_out, M11_out, nand_1_out);
  or P2 (P[2], and_4_out, and_5_out, and_6_out);
  or or_3 (or_3_out, A[2], A[0]);
  nor nor_1 (nor_1_out, B[2], A[2]);
  and and_6 (and_6_out, P[0], nor_1_out);
  nand nand_1 (nand_1_out, or_2_out, or_3_out, P[0]);
  and and_7 (and_7_out, A[1], ~A[0]);  // AND_Gate
  or or_4 (or_4_out, M10_out, and_7_out);
  and P3 (P[3], X22_out, or_4_out);
  and and_8 (and_8_out, B[2], A[2]);
  or A10 (A10_out, A[1], A[0]);
  or B10 (B10_out, B[1], B[0]);
  and and_9 (and_9_out, A10_out, X22_out);
  nor nor_2 (nor_2_out, B10_out, A10_out);
  and and_10 (and_10_out, and_8_out, nor_2_out);
  or P5 (P[5], and_9_out, and_12_out);
  or P4 (P[4], and_10_out, P[5]);
  and and_11 (and_11_out, ~B[2], A[2]);  // AND_Gate
  and and_12 (and_12_out, B10_out, and_11_out);
endmodule

module check (
  output [3:0] out_1,
  output [3:0] out_2,
  output [3:0] out_3,
  output [3:0] out_4,
  output [3:0] out_5,
  output [3:0] out_6,
  output [3:0] out_7,
  output [3:0] out_8,
  output [3:0] out_9,
  output [3:0] out_10,
  output [3:0] out_11,
  output [3:0] out_12,
  output [3:0] out_13,
  output [3:0] out_14,
  output [3:0] out_15,
  output [3:0] out_16,
  output [3:0] out_17,
  output [3:0] out_18,
  output [3:0] out_19,
  output [3:0] out_20,
  output [3:0] out_21,
  output [3:0] out_22,
  output [3:0] out_23,
  output [3:0] out_24,
  output [3:0] out_25,
  output [3:0] out_26,
  output [3:0] out_27,
  output [3:0] out_28,
  output [3:0] out_29,
  output [3:0] out_30,
  output [3:0] out_31,
  output [3:0] out_32,
  output [3:0] out_33,
  output [3:0] out_34,
  output [3:0] out_35,
  output [3:0] out_36,
  output [3:0] out_37,
  output [3:0] out_38,
  output [3:0] out_39,
  output [3:0] out_40,
  output [3:0] out_41,
  output [3:0] out_42,
  output [3:0] out_43,
  output [3:0] out_44,
  output [3:0] out_45,
  output [3:0] out_46,
  output [3:0] out_47,
  output [3:0] out_48,
  output [3:0] out_49,
  output [3:0] out_50,
  output [3:0] out_51,
  output [3:0] out_52,
  output [3:0] out_53,
  output [3:0] out_54,
  output [3:0] out_55,
  output [3:0] out_56,
  output [3:0] out_57,
  output [3:0] out_58,
  output [3:0] out_59,
  output [3:0] out_60,
  output [3:0] out_61,
  output [3:0] out_62,
  output [3:0] out_63,
  output [3:0] out_64
);

  mult mult_1 (.A(2'b00), .B(2'b00), .P(out_1));
  mult mult_2 (.A(2'b00), .B(2'b01), .P(out_9));
  mult mult_3 (.A(2'b00), .B(2'b10), .P(out_17));
  mult mult_4 (.A(2'b00), .B(2'b11), .P(out_23));
  mult mult_5 (.A(2'b01), .B(2'b00), .P(out_31));
  mult mult_6 (.A(2'b01), .B(2'b01), .P(out_37));
  mult mult_7 (.A(2'b01), .B(2'b10), .P(out_45));
  mult mult_8 (.A(2'b01), .B(2'b11), .P(out_53));
  mult mult_9 (.A(2'b10), .B(2'b00), .P(out_2));
  mult mult_10 (.A(2'b10), .B(2'b01), .P(out_10));
  mult mult_11 (.A(2'b10), .B(2'b10), .P(out_18));
  mult mult_12 (.A(2'b10), .B(2'b11), .P(out_24));
  mult mult_13 (.A(2'b11), .B(2'b00), .P(out_32));
  mult mult_14 (.A(2'b11), .B(2'b01), .P(out_38));
  mult mult_15 (.A(2'b11), .B(2'b10), .P(out_46));
  mult mult_16 (.A(2'b11), .B(2'b11), .P(out_54));
  two_1 b00x00 (.A(2'b00), .B(2'b00), .M(out_3), .SGN(out_7));
  two_1 b01x01 (.A(2'b01), .B(2'b01), .M(out_11), .SGN(out_15));
  two_1 b00x01 (.A(2'b00), .B(2'b01), .M(out_21), .SGN(out_25));
  two_1 b00x10 (.A(2'b00), .B(2'b10), .M(out_29), .SGN(out_33));
  two_1 b00x11 (.A(2'b00), .B(2'b11), .M(out_39), .SGN(out_43));
  two_1 b01x10 (.A(2'b01), .B(2'b10), .M(out_47), .SGN(out_51));
  two_1 b01x11 (.A(2'b01), .B(2'b11), .M(out_57), .SGN(out_59));
  two_1 b10x11 (.A(2'b10), .B(2'b11), .M(out_61), .SGN(out_63));
  two_2 b10x10 (.M(out_4), .SGN(out_8), .A(2'b10), .B(2'b10));
  two_2 b11x11 (.M(out_12), .SGN(out_16), .A(2'b11), .B(2'b11));
  two_2 b01x00 (.M(out_22), .SGN(out_26), .A(2'b01), .B(2'b00));
  two_2 b10x00 (.M(out_30), .SGN(out_34), .A(2'b10), .B(2'b00));
  two_2 b11x00 (.M(out_40), .SGN(out_44), .A(2'b11), .B(2'b00));
  two_2 b10x01 (.M(out_48), .SGN(out_52), .A(2'b10), .B(2'b01));
  two_2 b11x01 (.M(out_58), .SGN(out_60), .A(2'b11), .B(2'b01));
  two_2 b11x10 (.M(out_62), .SGN(out_64), .A(2'b11), .B(2'b10));

  assign out_5 = out_1;
  assign out_6 = out_2;
  assign out_13 = out_9;
  assign out_14 = out_10;
  assign out_19 = out_17;
  assign out_20 = out_18;
  assign out_27 = out_23;
  assign out_28 = out_24;
  assign out_35 = out_31;
  assign out_36 = out_32;
  assign out_41 = out_37;
  assign out_42 = out_38;
  assign out_49 = out_45;
  assign out_50 = out_46;
  assign out_55 = out_53;
  assign out_56 = out_54;
endmodule

module op (
  input  [1:0] A,
  input  [1:0] B,
  input  sgn,
  output [3:0] P
);

  wire decoder_1_out0, decoder_1_out1;
  wire [3:0] and_1_out, and_2_out, bit_extender_1_out, bit_extender_2_out, mult_1_p, mult_sgn_1_p;

  Decoder decoder_1 (.out0(decoder_1_out0), .out1(decoder_1_out1), .sel(sgn), .en(1'b1));
  mult mult_1 (.A(A), .B(B), .P(mult_1_p));
  assign bit_extender_1_out = {{3{decoder_1_out0}}, decoder_1_out0};  // Bit_Extender bit_extender_1
  mult_sgn mult_sgn_1 (.A(A), .B(B), .P(mult_sgn_1_p));
  assign bit_extender_2_out = {{3{decoder_1_out1}}, decoder_1_out1};  // Bit_Extender bit_extender_2
  assign and_1_out = mult_1_p & bit_extender_1_out;  // AND_Gate and_1, 4 bits wide
  assign and_2_out = mult_sgn_1_p & bit_extender_2_out;  // AND_Gate and_2, 4 bits wide
  assign P = and_1_out | and_2_out;  // OR_Gate or_1, 4 bits wide

  // Notes on the sheet:
  //   M
  //   +-
endmodule

module two_1 (
  input  [1:0] A,
  input  [1:0] B,
  output [3:0] M,
  output [3:0] SGN
);

  mult mult_1 (.A(A), .B(B), .P(M));
  mult_sgn mult_sgn_1 (.A(A), .B(B), .P(SGN));
endmodule

module two_2 (
  input  [1:0] A,
  input  [1:0] B,
  output [3:0] M,
  output [3:0] SGN
);

  mult mult_1 (.A(A), .B(B), .P(M));
  mult_sgn mult_sgn_1 (.A(A), .B(B), .P(SGN));
endmodule

module HA (
  input  B,
  input  A,
  output s,
  output Cout
);

  xor xor_1 (s, B, A);
  and and_1 (Cout, B, A);
endmodule

module FA (
  input  Cin,
  input  B,
  input  A,
  output s,
  output Cout
);

  wire ha_1_cout, ha_1_s, ha_2_cout;

  HA ha_1 (.B(B), .A(A), .s(ha_1_s), .Cout(ha_1_cout));
  HA ha_2 (.B(Cin), .A(ha_1_s), .s(s), .Cout(ha_2_cout));
  or or_1 (Cout, ha_2_cout, ha_1_cout);
endmodule

module mult4 (
  input  [3:0] A,
  input  [3:0] B,
  output [7:0] P
);

  wire and_2_out, and_3_out, and_4_out, and_5_out, and_6_out, and_7_out, and_8_out, and_9_out, and_10_out,
       and_11_out, and_12_out, and_13_out, and_14_out, and_15_out, and_16_out, fa_1_cout, fa_2_cout, fa_2_s,
       fa_3_cout, fa_4_cout, fa_4_s, fa_5_cout, fa_6_cout, fa_7_cout, fa_7_s, ha_1_cout, ha_2_cout, ha_2_s,
       ha_3_cout, ha_3_s, ha_4_cout, ha_4_s;

  and and_1 (P[0], B[0], A[0]);
  and and_2 (and_2_out, B[1], A[0]);
  and and_3 (and_3_out, B[0], A[1]);
  HA ha_1 (.B(and_2_out), .A(and_3_out), .s(P[1]), .Cout(ha_1_cout));
  and and_4 (and_4_out, B[2], A[0]);
  and and_5 (and_5_out, B[1], A[1]);
  HA ha_2 (.B(and_4_out), .A(and_5_out), .s(ha_2_s), .Cout(ha_2_cout));
  FA fa_1 (.Cin(ha_1_cout), .B(ha_2_s), .A(and_6_out), .s(P[2]), .Cout(fa_1_cout));
  and and_6 (and_6_out, B[0], A[2]);
  and and_7 (and_7_out, B[3], A[0]);
  and and_8 (and_8_out, B[2], A[1]);
  HA ha_3 (.B(and_7_out), .A(and_8_out), .s(ha_3_s), .Cout(ha_3_cout));
  FA fa_2 (.Cin(ha_2_cout), .B(ha_3_s), .A(and_9_out), .s(fa_2_s), .Cout(fa_2_cout));
  FA fa_3 (.Cin(fa_1_cout), .B(fa_2_s), .A(and_10_out), .s(P[3]), .Cout(fa_3_cout));
  and and_9 (and_9_out, B[1], A[2]);
  and and_10 (and_10_out, B[0], A[3]);
  and and_11 (and_11_out, B[3], A[1]);
  FA fa_4 (.Cin(ha_3_cout), .B(ha_4_s), .A(and_13_out), .s(fa_4_s), .Cout(fa_4_cout));
  FA fa_5 (.Cin(fa_3_cout), .B(fa_2_cout), .A(fa_4_s), .s(P[4]), .Cout(fa_5_cout));
  and and_12 (and_12_out, B[2], A[2]);
  and and_13 (and_13_out, B[1], A[3]);
  HA ha_4 (.B(and_11_out), .A(and_12_out), .s(ha_4_s), .Cout(ha_4_cout));
  FA fa_6 (.Cin(fa_5_cout), .B(fa_4_cout), .A(fa_7_s), .s(P[5]), .Cout(fa_6_cout));
  and and_14 (and_14_out, B[3], A[2]);
  and and_15 (and_15_out, B[2], A[3]);
  and and_16 (and_16_out, B[3], A[3]);
  FA fa_7 (.Cin(ha_4_cout), .B(and_14_out), .A(and_15_out), .s(fa_7_s), .Cout(fa_7_cout));
  FA fa_8 (.Cin(fa_6_cout), .B(fa_7_cout), .A(and_16_out), .s(P[6]), .Cout(P[7]));
endmodule

module mult4_HA (
  input  [3:0] A,
  input  [3:0] B,
  output [7:0] P
);

  wire and_2_out, and_3_out, and_4_out, and_5_out, and_6_out, and_7_out, and_8_out, and_9_out, and_10_out,
       and_11_out, and_12_out, and_13_out, and_14_out, and_15_out, and_16_out, fa_1_cout, fa_1_s, fa_2_cout,
       fa_2_s, fa_3_cout, fa_3_s, fa_4_cout, fa_4_s, fa_5_cout, fa_5_s, fa_6_cout, fa_6_s, fa_7_cout,
       ha_1_cout, ha_2_cout, ha_3_cout, ha_4_cout;

  and and_1 (P[0], B[0], A[0]);
  and and_2 (and_2_out, B[1], A[0]);
  and and_3 (and_3_out, B[0], A[1]);
  HA ha_1 (.B(and_2_out), .A(and_3_out), .s(P[1]), .Cout(ha_1_cout));
  and and_4 (and_4_out, B[2], A[0]);
  and and_5 (and_5_out, B[1], A[1]);
  FA fa_1 (.Cin(and_4_out), .B(and_5_out), .A(and_6_out), .s(fa_1_s), .Cout(fa_1_cout));
  HA ha_2 (.B(ha_1_cout), .A(fa_1_s), .s(P[2]), .Cout(ha_2_cout));
  and and_6 (and_6_out, B[0], A[2]);
  and and_7 (and_7_out, B[3], A[0]);
  and and_8 (and_8_out, B[2], A[1]);
  FA fa_2 (.Cin(and_7_out), .B(and_8_out), .A(and_9_out), .s(fa_2_s), .Cout(fa_2_cout));
  FA fa_3 (.Cin(fa_1_cout), .B(fa_2_s), .A(and_10_out), .s(fa_3_s), .Cout(fa_3_cout));
  HA ha_3 (.B(ha_2_cout), .A(fa_3_s), .s(P[3]), .Cout(ha_3_cout));
  and and_9 (and_9_out, B[1], A[2]);
  and and_10 (and_10_out, B[0], A[3]);
  and and_11 (and_11_out, B[3], A[1]);
  FA fa_4 (.Cin(fa_3_cout), .B(fa_2_cout), .A(fa_5_s), .s(fa_4_s), .Cout(fa_4_cout));
  HA ha_4 (.B(ha_3_cout), .A(fa_4_s), .s(P[4]), .Cout(ha_4_cout));
  and and_12 (and_12_out, B[2], A[2]);
  and and_13 (and_13_out, B[1], A[3]);
  FA fa_5 (.Cin(and_11_out), .B(and_12_out), .A(and_13_out), .s(fa_5_s), .Cout(fa_5_cout));
  FA fa_6 (.Cin(fa_5_cout), .B(and_14_out), .A(and_15_out), .s(fa_6_s), .Cout(fa_6_cout));
  FA fa_7 (.Cin(ha_4_cout), .B(fa_4_cout), .A(fa_6_s), .s(P[5]), .Cout(fa_7_cout));
  and and_14 (and_14_out, B[3], A[2]);
  and and_15 (and_15_out, B[2], A[3]);
  and and_16 (and_16_out, B[3], A[3]);
  FA fa_8 (.Cin(fa_7_cout), .B(fa_6_cout), .A(and_16_out), .s(P[6]), .Cout(P[7]));
endmodule
